// Digital circuit 2 bit multiplier.dig as structural Verilog
module _2_bit_multiplier (
  input  A1,
  input  A0,
  input  B0,
  input  B1,
  output out_5,
  output out_6,
  output out_7,
  output out_8
);

  wire and_2_out, and_3_out, and_4_out, and_5_out;

  and and_1 (out_5, A0, B0);
  and and_2 (and_2_out, A0, B1);
  and and_3 (and_3_out, A1, B0);
  and and_4 (and_4_out, A1, B1);
  and and_5 (and_5_out, A0, B0, B1);
  and and_6 (out_8, A1, B1, A0, B0);
  xor xor_1 (out_6, and_2_out, and_3_out);
  xor xor_2 (out_7, and_4_out, and_5_out);
endmodule
